# Fritzing sketch Teammaster 5000 Sketch (saved by Fritzing 0.9.3b)
breadboards: 1

parts:
  LCD1 = LCD screen
  Bauteil1 = Arduino Nano (Rev3.0)
  Bestätigen = Pushbutton [package="[THT]"]
  Abbruch = Pushbutton [package="[THT]"]
  SPKR1 = Loudspeaker
  R1 = Trimmer Potentiometer [maximum_resistance=10kΩ package=THT]
  R2 = Resistor [tolerance=±5% resistance=220 package=THT]
  J1 = Basic Servo

nets:
  GND: LCD1.VSS, LCD1.V0, LCD1.R/W, LCD1.LED-, Bauteil1.GND, Bestätigen.Pin_3, Bestätigen.Pin_4, Abbruch.Pin_3, Abbruch.Pin_4, SPKR1.pin1, R1.leg1, J1.gnd
  VDD: LCD1.VDD, Bauteil1.5V, R1.leg2, R2.Pin_0, J1.vcc
  N1: LCD1.RS, Bauteil1.D12/MISO
  N2: LCD1.E, Bauteil1.D11/MOSI
  N3: LCD1.DB4, Bauteil1.D5
  N4: LCD1.DB5, Bauteil1.D4
  N5: LCD1.DB6, Bauteil1.D3
  N6: LCD1.DB7, Bauteil1.D2
  N7: LCD1.LED+, R2.Pin_1
  N8: Bauteil1.D6, Bestätigen.Pin_1, Bestätigen.Pin_2
  N9: Bauteil1.D8, SPKR1.pin2
  N10: Bauteil1.D9, J1.pulse
  N11: Bauteil1.D10, Abbruch.Pin_1, Abbruch.Pin_2
  N12: Bauteil1.A0, R1.wiper
